// Logisim project calculatrice.circ as structural Verilog: 4 circuits, main circuit main
module main (
  input  D1,
  input  D2,
  input  C1,
  input  C2,
  input  B1,
  input  B2,
  input  A1,
  input  A2,
  input  com
);

  wire addisous_1_rs, addisous_1_s, addisous_2_rs, addisous_2_s, addisous_3_rs, addisous_3_s, addisous_4_rs,
       addisous_4_s, fusion_1_a_2, fusion_1_b_2, fusion_1_c_2, fusion_1_d_2, fusion_1_e, fusion_1_f,
       fusion_1_g, fusion_2_a_2, fusion_2_b_2, fusion_2_c_2, fusion_2_d_2, fusion_2_e, fusion_2_f,
       fusion_2_g, fusion_3_a_2, fusion_3_b_2, fusion_3_c_2, fusion_3_d_2, fusion_3_e, fusion_3_f, fusion_3_g;

  LED \dépassement  (.in(addisous_1_rs));
  Fusion fusion_1 (
    .A(A1), .B(B1), .C(C1), .D(D1), .a_2(fusion_1_a_2), .b_2(fusion_1_b_2), .c_2(fusion_1_c_2),
    .d_2(fusion_1_d_2), .e(fusion_1_e), .f(fusion_1_f), .g(fusion_1_g));
  _7_Segment_Display u_7_segment_display_1 (
    .g(fusion_1_g), .f(fusion_1_f), .a(fusion_1_a_2), .b(fusion_1_b_2), .e(fusion_1_e), .d(fusion_1_d_2),
    .c(fusion_1_c_2));  // open: dp
  AddiSous addisous_1 (.C(com), .A(A1), .B(A2), .Re(addisous_2_rs), .S(addisous_1_s), .Rs(addisous_1_rs));
  AddiSous addisous_2 (.C(com), .A(B1), .B(B2), .Re(addisous_3_rs), .S(addisous_2_s), .Rs(addisous_2_rs));
  AddiSous addisous_3 (.C(com), .A(C1), .B(C2), .Re(addisous_4_rs), .S(addisous_3_s), .Rs(addisous_3_rs));
  Fusion fusion_2 (
    .A(A2), .B(B2), .C(C2), .D(D2), .a_2(fusion_2_a_2), .b_2(fusion_2_b_2), .c_2(fusion_2_c_2),
    .d_2(fusion_2_d_2), .e(fusion_2_e), .f(fusion_2_f), .g(fusion_2_g));
  Fusion fusion_3 (
    .A(addisous_1_s), .B(addisous_2_s), .C(addisous_3_s), .D(addisous_4_s), .a_2(fusion_3_a_2),
    .b_2(fusion_3_b_2), .c_2(fusion_3_c_2), .d_2(fusion_3_d_2), .e(fusion_3_e), .f(fusion_3_f), .g(fusion_3_g));
  _7_Segment_Display u_7_segment_display_2 (
    .g(fusion_2_g), .f(fusion_2_f), .a(fusion_2_a_2), .b(fusion_2_b_2), .e(fusion_2_e), .d(fusion_2_d_2),
    .c(fusion_2_c_2));  // open: dp
  AddiSous addisous_4 (.C(com), .A(D1), .B(D2), .Re(1'b0), .S(addisous_4_s), .Rs(addisous_4_rs));
  _7_Segment_Display u_7_segment_display_3 (
    .g(fusion_3_g), .f(fusion_3_f), .a(fusion_3_a_2), .b(fusion_3_b_2), .e(fusion_3_e), .d(fusion_3_d_2),
    .c(fusion_3_c_2));  // open: dp
endmodule

module DemiAddiSous (
  input  A,
  input  B,
  input  C,
  output S,
  output Rs
);

  wire xor_1_out;

  xor xor_1 (xor_1_out, A, C);
  xor xor_2 (S, A, B);
  and and_1 (Rs, B, xor_1_out);
endmodule

module AddiSous (
  input  C,
  input  A,
  input  B,
  input  Re,
  output S,
  output Rs
);

  wire demiaddisous_1_rs, demiaddisous_1_s, demiaddisous_2_rs;

  DemiAddiSous demiaddisous_1 (.A(A), .B(B), .C(C), .S(demiaddisous_1_s), .Rs(demiaddisous_1_rs));
  DemiAddiSous demiaddisous_2 (.A(demiaddisous_1_s), .B(Re), .C(C), .S(S), .Rs(demiaddisous_2_rs));
  or or_1 (Rs, demiaddisous_2_rs, demiaddisous_1_rs);
endmodule

module Fusion (
  input  A,
  input  B,
  input  C,
  input  D,
  output a_2,
  output b_2,
  output c_2,
  output d_2,
  output e,
  output f,
  output g
);

  wire and_1_out, and_2_out, and_3_out, and_4_out, and_5_out, and_6_out, and_7_out, and_8_out, and_9_out,
       and_10_out, and_11_out, and_12_out, and_13_out, and_14_out, and_15_out, and_16_out, not_1_out,
       not_2_out, not_3_out, not_4_out, not_5_out, not_6_out, not_7_out, not_8_out, not_9_out, not_10_out,
       not_11_out, not_12_out, not_13_out, not_14_out, not_15_out, not_16_out;

  not not_1 (not_1_out, B);
  not not_2 (not_2_out, C);
  not not_3 (not_3_out, B);
  not not_4 (not_4_out, D);
  not not_5 (not_5_out, C);
  not not_6 (not_6_out, B);
  not not_7 (not_7_out, D);
  not not_8 (not_8_out, C);
  not not_9 (not_9_out, D);
  not not_10 (not_10_out, B);
  not not_11 (not_11_out, D);
  not not_12 (not_12_out, C);
  and and_1 (and_1_out, B, D);
  not not_13 (not_13_out, B);
  not not_14 (not_14_out, D);
  and and_2 (and_2_out, C, D);
  and and_3 (and_3_out, not_3_out, C);
  and and_4 (and_4_out, C, not_4_out);
  and and_5 (and_5_out, B, not_5_out, D);
  and and_6 (and_6_out, not_6_out, not_7_out);
  and and_7 (and_7_out, not_7_out, C);
  and and_8 (and_8_out, B, not_8_out);
  and and_9 (and_9_out, not_8_out, not_9_out);
  and and_10 (and_10_out, not_9_out, B);
  and and_11 (and_11_out, not_10_out, C);
  and and_12 (and_12_out, C, not_11_out);
  and and_13 (and_13_out, not_12_out, B);
  and and_14 (and_14_out, not_13_out, not_14_out);
  not not_15 (not_15_out, C);
  not not_16 (not_16_out, D);
  and and_15 (and_15_out, not_3_out, not_4_out);
  and and_16 (and_16_out, not_15_out, not_16_out);
  or or_1 (a_2, and_1_out, C, A, and_14_out);
  or or_2 (b_2, A, not_1_out, and_2_out, and_16_out);
  or or_3 (c_2, A, B, not_2_out, D);
  or or_4 (d_2, A, and_3_out, and_4_out, and_15_out, and_5_out);
  or or_5 (e, and_6_out, and_7_out);
  or or_6 (f, A, and_8_out, and_9_out, and_10_out);
  or or_7 (g, A, and_11_out, and_12_out, and_13_out);
endmodule
