// Logisim project calculatrice_v2.circ as structural Verilog: 10 circuits, main circuit main
module main (
  input  in_1,
  input  in_2,
  input  in_3,
  input  in_4,
  input  in_5,
  input  in_6,
  input  in_7,
  input  in_8,
  input  in_9,
  input  in_10,
  input  in_11,
  input  in_12,
  input  in_13,
  input  in_14,
  input  in_15,
  input  in_16,
  input  in_17,
  input  in_18,
  input  in_19,
  input  in_20,
  input  in_21,
  input  in_22,
  input  in_23,
  input  in_24,
  input  in_25,
  input  in_26,
  input  in_27,
  input  in_28,
  input  in_29,
  input  in_30,
  input  in_31,
  input  in_32,
  input  in_33
);

  wire [6:0] afficheur_16_bits_1_out_5, afficheur_16_bits_1_out_5_2, afficheur_16_bits_2_out_5,
       afficheur_16_bits_2_out_5_2, n16bits_addi_sous_1_out_4, n16bits_addi_sous_1_out_5,
       n16bits_addi_sous_1_out_6, n16bits_addi_sous_1_out_7, n16bits_addi_sous_1_out_8;
  wire [13:0] afficheur_16_bits_1_out_2, afficheur_16_bits_1_out_3, afficheur_16_bits_1_out_4,
       afficheur_16_bits_2_out_2, afficheur_16_bits_2_out_3, afficheur_16_bits_2_out_4;

  _7_Segment_Display u_7_segment_display_1 (
    .g(afficheur_16_bits_1_out_5_2[0]), .f(afficheur_16_bits_1_out_5_2[1]),
    .a(afficheur_16_bits_1_out_5_2[6]), .b(afficheur_16_bits_1_out_5_2[5]),
    .e(afficheur_16_bits_1_out_5_2[2]), .d(afficheur_16_bits_1_out_5_2[3]), .c(afficheur_16_bits_1_out_5_2[4]));  // open: dp
  _7_Segment_Display u_7_segment_display_2 (
    .g(afficheur_16_bits_2_out_5_2[0]), .f(afficheur_16_bits_2_out_5_2[1]),
    .a(afficheur_16_bits_2_out_5_2[6]), .b(afficheur_16_bits_2_out_5_2[5]),
    .e(afficheur_16_bits_2_out_5_2[2]), .d(afficheur_16_bits_2_out_5_2[3]), .c(afficheur_16_bits_2_out_5_2[4]));  // open: dp
  _7_Segment_Display u_7_segment_display_3 (
    .g(afficheur_16_bits_1_out_5[0]), .f(afficheur_16_bits_1_out_5[1]), .a(afficheur_16_bits_1_out_5[6]),
    .b(afficheur_16_bits_1_out_5[5]), .e(afficheur_16_bits_1_out_5[2]), .d(afficheur_16_bits_1_out_5[3]),
    .c(afficheur_16_bits_1_out_5[4]));  // open: dp
  _7_Segment_Display u_7_segment_display_4 (
    .g(afficheur_16_bits_2_out_5[0]), .f(afficheur_16_bits_2_out_5[1]), .a(afficheur_16_bits_2_out_5[6]),
    .b(afficheur_16_bits_2_out_5[5]), .e(afficheur_16_bits_2_out_5[2]), .d(afficheur_16_bits_2_out_5[3]),
    .c(afficheur_16_bits_2_out_5[4]));  // open: dp
  _7_Segment_Display u_7_segment_display_5 (
    .g(afficheur_16_bits_1_out_4[7]), .f(afficheur_16_bits_1_out_4[8]), .a(afficheur_16_bits_1_out_4[13]),
    .b(afficheur_16_bits_1_out_4[12]), .e(afficheur_16_bits_1_out_4[9]), .d(afficheur_16_bits_1_out_4[10]),
    .c(afficheur_16_bits_1_out_4[11]));  // open: dp
  Afficheur_16_bits afficheur_16_bits_1 (
    .in_1({in_1, in_2, in_3, in_4, in_5, in_6, in_7, in_8, in_9, in_10, in_11, in_12, in_13, in_14, in_15, in_16}),
    .out_2(afficheur_16_bits_1_out_2), .out_3(afficheur_16_bits_1_out_3), .out_4(afficheur_16_bits_1_out_4),
    .out_5({afficheur_16_bits_1_out_5_2, afficheur_16_bits_1_out_5}));
  Afficheur_16_bits afficheur_16_bits_2 (
    .in_1({in_18, in_19, in_20, in_21, in_22, in_23, in_24, in_25, in_26, in_27, in_28, in_29, in_30, in_31, in_32, in_33}),
    .out_2(afficheur_16_bits_2_out_2), .out_3(afficheur_16_bits_2_out_3), .out_4(afficheur_16_bits_2_out_4),
    .out_5({afficheur_16_bits_2_out_5_2, afficheur_16_bits_2_out_5}));
  _7_Segment_Display u_7_segment_display_6 (
    .g(afficheur_16_bits_2_out_4[7]), .f(afficheur_16_bits_2_out_4[8]), .a(afficheur_16_bits_2_out_4[13]),
    .b(afficheur_16_bits_2_out_4[12]), .e(afficheur_16_bits_2_out_4[9]), .d(afficheur_16_bits_2_out_4[10]),
    .c(afficheur_16_bits_2_out_4[11]));  // open: dp
  _7_Segment_Display u_7_segment_display_7 (
    .g(afficheur_16_bits_1_out_4[0]), .f(afficheur_16_bits_1_out_4[1]), .a(afficheur_16_bits_1_out_4[6]),
    .b(afficheur_16_bits_1_out_4[5]), .e(afficheur_16_bits_1_out_4[2]), .d(afficheur_16_bits_1_out_4[3]),
    .c(afficheur_16_bits_1_out_4[4]));  // open: dp
  _7_Segment_Display u_7_segment_display_8 (
    .g(afficheur_16_bits_2_out_4[0]), .f(afficheur_16_bits_2_out_4[1]), .a(afficheur_16_bits_2_out_4[6]),
    .b(afficheur_16_bits_2_out_4[5]), .e(afficheur_16_bits_2_out_4[2]), .d(afficheur_16_bits_2_out_4[3]),
    .c(afficheur_16_bits_2_out_4[4]));  // open: dp
  _7_Segment_Display u_7_segment_display_9 (
    .g(afficheur_16_bits_1_out_3[7]), .f(afficheur_16_bits_1_out_3[8]), .a(afficheur_16_bits_1_out_3[13]),
    .b(afficheur_16_bits_1_out_3[12]), .e(afficheur_16_bits_1_out_3[9]), .d(afficheur_16_bits_1_out_3[10]),
    .c(afficheur_16_bits_1_out_3[11]));  // open: dp
  _7_Segment_Display u_7_segment_display_10 (
    .g(afficheur_16_bits_2_out_3[7]), .f(afficheur_16_bits_2_out_3[8]), .a(afficheur_16_bits_2_out_3[13]),
    .b(afficheur_16_bits_2_out_3[12]), .e(afficheur_16_bits_2_out_3[9]), .d(afficheur_16_bits_2_out_3[10]),
    .c(afficheur_16_bits_2_out_3[11]));  // open: dp
  _7_Segment_Display u_7_segment_display_11 (
    .g(afficheur_16_bits_1_out_3[0]), .f(afficheur_16_bits_1_out_3[1]), .a(afficheur_16_bits_1_out_3[6]),
    .b(afficheur_16_bits_1_out_3[5]), .e(afficheur_16_bits_1_out_3[2]), .d(afficheur_16_bits_1_out_3[3]),
    .c(afficheur_16_bits_1_out_3[4]));  // open: dp
  _7_Segment_Display u_7_segment_display_12 (
    .g(afficheur_16_bits_2_out_3[0]), .f(afficheur_16_bits_2_out_3[1]), .a(afficheur_16_bits_2_out_3[6]),
    .b(afficheur_16_bits_2_out_3[5]), .e(afficheur_16_bits_2_out_3[2]), .d(afficheur_16_bits_2_out_3[3]),
    .c(afficheur_16_bits_2_out_3[4]));  // open: dp
  _7_Segment_Display u_7_segment_display_13 (
    .g(afficheur_16_bits_1_out_2[7]), .f(afficheur_16_bits_1_out_2[8]), .a(afficheur_16_bits_1_out_2[13]),
    .b(afficheur_16_bits_1_out_2[12]), .e(afficheur_16_bits_1_out_2[9]), .d(afficheur_16_bits_1_out_2[10]),
    .c(afficheur_16_bits_1_out_2[11]));  // open: dp
  _7_Segment_Display u_7_segment_display_14 (
    .g(afficheur_16_bits_2_out_2[7]), .f(afficheur_16_bits_2_out_2[8]), .a(afficheur_16_bits_2_out_2[13]),
    .b(afficheur_16_bits_2_out_2[12]), .e(afficheur_16_bits_2_out_2[9]), .d(afficheur_16_bits_2_out_2[10]),
    .c(afficheur_16_bits_2_out_2[11]));  // open: dp
  _7_Segment_Display u_7_segment_display_15 (
    .g(afficheur_16_bits_1_out_2[0]), .f(afficheur_16_bits_1_out_2[1]), .a(afficheur_16_bits_1_out_2[6]),
    .b(afficheur_16_bits_1_out_2[5]), .e(afficheur_16_bits_1_out_2[2]), .d(afficheur_16_bits_1_out_2[3]),
    .c(afficheur_16_bits_1_out_2[4]));  // open: dp
  _7_Segment_Display u_7_segment_display_16 (
    .g(afficheur_16_bits_2_out_2[0]), .f(afficheur_16_bits_2_out_2[1]), .a(afficheur_16_bits_2_out_2[6]),
    .b(afficheur_16_bits_2_out_2[5]), .e(afficheur_16_bits_2_out_2[2]), .d(afficheur_16_bits_2_out_2[3]),
    .c(afficheur_16_bits_2_out_2[4]));  // open: dp
  _16Bits___Addi_Sous u_16bits_addi_sous_1 (
    .in_2({in_1, in_2, in_3, in_4, in_5, in_6, in_7, in_8, in_9, in_10, in_11, in_12, in_13, in_14, in_15, in_16}),
    .in_3({in_18, in_19, in_20, in_21, in_22, in_23, in_24, in_25, in_26, in_27, in_28, in_29, in_30, in_31, in_32, in_33}),
    .in_1(in_17), .out_4(n16bits_addi_sous_1_out_4), .out_5(n16bits_addi_sous_1_out_5),
    .out_6(n16bits_addi_sous_1_out_6), .out_7(n16bits_addi_sous_1_out_7), .out_8(n16bits_addi_sous_1_out_8));
  _7_Segment_Display u_7_segment_display_17 (
    .g(n16bits_addi_sous_1_out_8[0]), .f(n16bits_addi_sous_1_out_8[1]), .a(n16bits_addi_sous_1_out_8[6]),
    .b(n16bits_addi_sous_1_out_8[5]), .e(n16bits_addi_sous_1_out_8[2]), .d(n16bits_addi_sous_1_out_8[3]),
    .c(n16bits_addi_sous_1_out_8[4]));  // open: dp
  _7_Segment_Display u_7_segment_display_18 (
    .g(n16bits_addi_sous_1_out_7[0]), .f(n16bits_addi_sous_1_out_7[1]), .a(n16bits_addi_sous_1_out_7[6]),
    .b(n16bits_addi_sous_1_out_7[5]), .e(n16bits_addi_sous_1_out_7[2]), .d(n16bits_addi_sous_1_out_7[3]),
    .c(n16bits_addi_sous_1_out_7[4]));  // open: dp
  _7_Segment_Display u_7_segment_display_19 (
    .g(n16bits_addi_sous_1_out_6[0]), .f(n16bits_addi_sous_1_out_6[1]), .a(n16bits_addi_sous_1_out_6[6]),
    .b(n16bits_addi_sous_1_out_6[5]), .e(n16bits_addi_sous_1_out_6[2]), .d(n16bits_addi_sous_1_out_6[3]),
    .c(n16bits_addi_sous_1_out_6[4]));  // open: dp
  _7_Segment_Display u_7_segment_display_20 (
    .g(n16bits_addi_sous_1_out_5[0]), .f(n16bits_addi_sous_1_out_5[1]), .a(n16bits_addi_sous_1_out_5[6]),
    .b(n16bits_addi_sous_1_out_5[5]), .e(n16bits_addi_sous_1_out_5[2]), .d(n16bits_addi_sous_1_out_5[3]),
    .c(n16bits_addi_sous_1_out_5[4]));  // open: dp
  _7_Segment_Display u_7_segment_display_21 (
    .g(n16bits_addi_sous_1_out_4[0]), .f(n16bits_addi_sous_1_out_4[1]), .a(n16bits_addi_sous_1_out_4[6]),
    .b(n16bits_addi_sous_1_out_4[5]), .e(n16bits_addi_sous_1_out_4[2]), .d(n16bits_addi_sous_1_out_4[3]),
    .c(n16bits_addi_sous_1_out_4[4]));  // open: dp

  // Notes on the sheet:
  //   Selection (0= Addi / 1 = Sous)
endmodule

module Demi_ADD_Sous (
  input  in_1,
  input  in_2,
  input  in_3,
  output out_4,
  output out_5
);

  wire xor_1_out;

  xor xor_1 (xor_1_out, in_2, in_1);
  xor xor_2 (out_4, in_2, in_3);
  and and_1 (out_5, in_3, xor_1_out);
endmodule

module Fulll_Add_Sous (
  input  in_1,
  input  in_2,
  input  in_3,
  input  in_4,
  output out_5,
  output out_6
);

  wire demi_add_sous_1_out_4, demi_add_sous_1_out_5, demi_add_sous_2_out_5;

  Demi_ADD_Sous demi_add_sous_1 (
    .in_2(in_3), .in_3(in_4), .in_1(in_2), .out_4(demi_add_sous_1_out_4), .out_5(demi_add_sous_1_out_5));
  Demi_ADD_Sous demi_add_sous_2 (
    .in_2(demi_add_sous_1_out_4), .in_3(in_1), .in_1(in_2), .out_4(out_5), .out_5(demi_add_sous_2_out_5));
  or or_1 (out_6, demi_add_sous_2_out_5, demi_add_sous_1_out_5);
endmodule

module _4Bits_Add__Sous (
  input  in_1,
  input  in_2,
  input  in_3,
  input  in_4,
  input  in_5,
  input  in_6,
  input  in_7,
  input  in_8,
  input  in_9,
  input  in_10,
  output out_11,
  output out_12,
  output out_13,
  output out_14,
  output out_15
);

  wire fulll_add_sous_2_out_6, fulll_add_sous_3_out_6, fulll_add_sous_4_out_6;

  Fulll_Add_Sous fulll_add_sous_1 (
    .in_2(in_1), .in_3(in_3), .in_4(in_2), .in_1(fulll_add_sous_2_out_6), .out_5(out_12), .out_6(out_11));
  Fulll_Add_Sous fulll_add_sous_2 (
    .in_2(in_1), .in_3(in_5), .in_4(in_4), .in_1(fulll_add_sous_3_out_6), .out_5(out_13),
    .out_6(fulll_add_sous_2_out_6));
  Fulll_Add_Sous fulll_add_sous_3 (
    .in_2(in_1), .in_3(in_7), .in_4(in_6), .in_1(fulll_add_sous_4_out_6), .out_5(out_14),
    .out_6(fulll_add_sous_3_out_6));
  Fulll_Add_Sous fulll_add_sous_4 (
    .in_2(in_1), .in_3(in_9), .in_4(in_8), .in_1(in_10), .out_5(out_15), .out_6(fulll_add_sous_4_out_6));
endmodule

module Afficheur (
  input  in_1,
  input  in_2,
  input  in_3,
  input  in_4,
  output a,
  output b,
  output out_7,
  output d,
  output out_9,
  output out_10,
  output out_11
);

  wire and_1_out, and_2_out, and_3_out, and_4_out, and_5_out, and_6_out, and_7_out, and_8_out, and_9_out,
       and_10_out, and_11_out, and_12_out, and_13_out, and_14_out, and_15_out, and_16_out, and_17_out,
       and_18_out, and_19_out, and_20_out, not_1_out, not_2_out, not_3_out, not_4_out, not_5_out, not_6_out,
       not_7_out, not_8_out, not_9_out, not_10_out, not_11_out, not_12_out, not_13_out, not_14_out,
       not_15_out, not_16_out, not_17_out, not_18_out, not_19_out, not_20_out, not_21_out, not_22_out,
       or_1_out, or_3_out, or_4_out, or_5_out, or_7_out, or_9_out, or_10_out, or_12_out, or_13_out,
       or_14_out, or_16_out, or_17_out, or_19_out, or_20_out, or_22_out;

  and and_1 (and_1_out, in_2, in_4);
  or or_1 (or_1_out, in_1, in_3);
  or or_2 (a, or_1_out, or_3_out);
  not not_1 (not_1_out, in_4);
  not not_2 (not_2_out, in_2);
  and and_2 (and_2_out, not_2_out, not_1_out);
  or or_3 (or_3_out, and_1_out, and_2_out);
  not not_3 (not_3_out, in_3);
  not not_4 (not_4_out, in_4);
  and and_3 (and_3_out, not_3_out, not_4_out);
  or or_4 (or_4_out, and_3_out, not_5_out, not_5_out);
  not not_5 (not_5_out, in_2);
  or or_5 (or_5_out, in_1, and_4_out);
  or or_6 (b, or_4_out, or_5_out);
  and and_4 (and_4_out, in_3, in_4);
  not not_6 (not_6_out, in_3);
  or or_7 (or_7_out, not_6_out, in_4);
  or or_8 (out_7, or_7_out, or_9_out);
  or or_9 (or_9_out, in_2, in_1);
  not not_7 (not_7_out, in_2);
  not not_8 (not_8_out, in_4);
  and and_5 (and_5_out, not_7_out, not_8_out);
  or or_10 (or_10_out, and_5_out, in_1);
  not not_9 (not_9_out, in_2);
  and and_6 (and_6_out, not_9_out, in_3);
  or or_11 (d, or_10_out, or_13_out);
  not not_10 (not_10_out, in_4);
  and and_7 (and_7_out, in_3, not_10_out);
  or or_12 (or_12_out, and_6_out, and_7_out);
  or or_13 (or_13_out, or_12_out, and_9_out);
  not not_11 (not_11_out, in_3);
  and and_8 (and_8_out, in_2, not_11_out);
  and and_9 (and_9_out, and_8_out, in_4);
  and and_10 (and_10_out, in_3, in_1);
  or or_14 (or_14_out, and_10_out, and_11_out);
  not not_12 (not_12_out, in_4);
  and and_11 (and_11_out, in_3, not_12_out);
  or or_15 (out_9, or_14_out, or_16_out);
  not not_13 (not_13_out, in_2);
  and and_12 (and_12_out, not_13_out, not_15_out);
  and and_13 (and_13_out, in_1, in_2);
  or or_16 (or_16_out, and_13_out, and_12_out);
  not not_14 (not_14_out, in_3);
  not not_15 (not_15_out, in_4);
  not not_16 (not_16_out, in_4);
  and and_14 (and_14_out, not_14_out, not_16_out);
  or or_17 (or_17_out, and_14_out, and_15_out);
  not not_17 (not_17_out, in_3);
  and and_15 (and_15_out, in_2, not_17_out);
  or or_18 (out_10, or_17_out, or_19_out);
  not not_18 (not_18_out, in_4);
  and and_16 (and_16_out, in_2, not_18_out);
  or or_19 (or_19_out, in_1, and_16_out);
  or or_20 (or_20_out, in_1, and_18_out);
  not not_19 (not_19_out, in_3);
  and and_17 (and_17_out, in_3, not_20_out);
  and and_18 (and_18_out, in_2, not_19_out);
  or or_21 (out_11, or_20_out, or_22_out);
  not not_20 (not_20_out, in_4);
  not not_21 (not_21_out, in_1);
  and and_19 (and_19_out, not_21_out, not_22_out);
  or or_22 (or_22_out, and_17_out, and_20_out);
  not not_22 (not_22_out, in_2);
  and and_20 (and_20_out, and_19_out, in_3);

  // Notes on the sheet:
  //   c
  //   e
  //   f
endmodule

module _16Bits___Addi_Sous (
  input  in_1,
  input  [15:0] in_2,
  input  [15:0] in_3,
  output [6:0] out_4,
  output [6:0] out_5,
  output [6:0] out_6,
  output [6:0] out_7,
  output [6:0] out_8
);

  wire comparateur_4_bits_1_s, comparateur_4_bits_2_s, comparateur_4_bits_3_s, comparateur_4_bits_4_s,
       n4bits_add_sous_1_out_11, n4bits_add_sous_2_out_11, n4bits_add_sous_3_out_11,
       n4bits_add_sous_4_out_11, n4bits_add_sous_5_out_12, n4bits_add_sous_5_out_13,
       n4bits_add_sous_5_out_14, n4bits_add_sous_5_out_15, n4bits_add_sous_6_out_12,
       n4bits_add_sous_6_out_13, n4bits_add_sous_6_out_14, n4bits_add_sous_6_out_15,
       n4bits_add_sous_7_out_12, n4bits_add_sous_7_out_13, n4bits_add_sous_7_out_14,
       n4bits_add_sous_7_out_15, n4bits_add_sous_8_out_12, n4bits_add_sous_8_out_13,
       n4bits_add_sous_8_out_14, n4bits_add_sous_8_out_15, not_1_out, not_2_out, not_3_out, not_4_out,
       or_1_out, or_2_out, or_3_out, or_4_out;
  wire [3:0] n4bits_add_sous_1_out_12, n4bits_add_sous_2_out_12, n4bits_add_sous_3_out_12,
       n4bits_add_sous_4_out_12;

  Comparateur_4_bits comparateur_4_bits_1 (
    .x3(n4bits_add_sous_4_out_12[0]), .x2(n4bits_add_sous_4_out_12[1]), .x1(n4bits_add_sous_4_out_12[2]),
    .x0(n4bits_add_sous_4_out_12[3]), .S(comparateur_4_bits_1_s));  // open: Z
  or or_1 (or_1_out, n4bits_add_sous_4_out_11, comparateur_4_bits_1_s);
  _4Bits_Add__Sous u_4bits_add_sous_1 (
    .in_1(in_1), .in_2(in_2[7]), .in_4(in_2[6]), .in_6(in_2[5]), .in_8(in_2[4]), .in_10(or_1_out),
    .out_11(n4bits_add_sous_1_out_11), .out_15(n4bits_add_sous_1_out_12[3]),
    .out_14(n4bits_add_sous_1_out_12[2]), .out_13(n4bits_add_sous_1_out_12[1]),
    .out_12(n4bits_add_sous_1_out_12[0]), .in_3(in_3[7]), .in_5(in_3[6]), .in_7(in_3[5]), .in_9(in_3[4]));
  Comparateur_4_bits comparateur_4_bits_2 (
    .x3(n4bits_add_sous_1_out_12[0]), .x2(n4bits_add_sous_1_out_12[1]), .x1(n4bits_add_sous_1_out_12[2]),
    .x0(n4bits_add_sous_1_out_12[3]), .S(comparateur_4_bits_2_s));  // open: Z
  or or_2 (or_2_out, n4bits_add_sous_1_out_11, comparateur_4_bits_2_s);
  _4Bits_Add__Sous u_4bits_add_sous_2 (
    .in_1(in_1), .in_2(in_2[11]), .in_4(in_2[10]), .in_6(in_2[9]), .in_8(in_2[8]), .in_10(or_2_out),
    .out_11(n4bits_add_sous_2_out_11), .out_15(n4bits_add_sous_2_out_12[3]),
    .out_14(n4bits_add_sous_2_out_12[2]), .out_13(n4bits_add_sous_2_out_12[1]),
    .out_12(n4bits_add_sous_2_out_12[0]), .in_3(in_3[11]), .in_5(in_3[10]), .in_7(in_3[9]), .in_9(in_3[8]));
  Comparateur_4_bits comparateur_4_bits_3 (
    .x3(n4bits_add_sous_2_out_12[0]), .x2(n4bits_add_sous_2_out_12[1]), .x1(n4bits_add_sous_2_out_12[2]),
    .x0(n4bits_add_sous_2_out_12[3]), .S(comparateur_4_bits_3_s));  // open: Z
  or or_3 (or_3_out, n4bits_add_sous_2_out_11, comparateur_4_bits_3_s);
  _4Bits_Add__Sous u_4bits_add_sous_3 (
    .in_1(in_1), .in_2(in_2[15]), .in_4(in_2[14]), .in_6(in_2[13]), .in_8(in_2[12]), .in_10(or_3_out),
    .out_11(n4bits_add_sous_3_out_11), .out_15(n4bits_add_sous_3_out_12[3]),
    .out_14(n4bits_add_sous_3_out_12[2]), .out_13(n4bits_add_sous_3_out_12[1]),
    .out_12(n4bits_add_sous_3_out_12[0]), .in_3(in_3[15]), .in_5(in_3[14]), .in_7(in_3[13]), .in_9(in_3[12]));
  Comparateur_4_bits comparateur_4_bits_4 (
    .x3(n4bits_add_sous_3_out_12[0]), .x2(n4bits_add_sous_3_out_12[1]), .x1(n4bits_add_sous_3_out_12[2]),
    .x0(n4bits_add_sous_3_out_12[3]), .S(comparateur_4_bits_4_s));  // open: Z
  or or_4 (or_4_out, n4bits_add_sous_3_out_11, comparateur_4_bits_4_s);
  _4Bits_Add__Sous u_4bits_add_sous_4 (
    .in_1(in_1), .in_2(in_2[3]), .in_4(in_2[2]), .in_6(in_2[1]), .in_8(in_2[0]), .in_10(1'b0),
    .out_11(n4bits_add_sous_4_out_11), .out_15(n4bits_add_sous_4_out_12[3]),
    .out_14(n4bits_add_sous_4_out_12[2]), .out_13(n4bits_add_sous_4_out_12[1]),
    .out_12(n4bits_add_sous_4_out_12[0]), .in_3(in_3[3]), .in_5(in_3[2]), .in_7(in_3[1]), .in_9(in_3[0]));
  not not_1 (not_1_out, in_1);
  Afficheur afficheur_1 (
    .in_1(1'b0), .in_2(1'b0), .in_3(1'b0), .in_4(or_4_out), .a(out_8[6]), .b(out_8[5]), .out_7(out_8[4]),
    .d(out_8[3]), .out_9(out_8[2]), .out_10(out_8[1]), .out_11(out_8[0]));
  not not_2 (not_2_out, in_1);
  _4Bits_Add__Sous u_4bits_add_sous_5 (
    .in_1(not_2_out), .in_2(or_1_out), .in_4(1'b0), .in_6(or_1_out), .in_8(1'b0), .in_10(1'b0),
    .out_15(n4bits_add_sous_5_out_15), .out_14(n4bits_add_sous_5_out_14), .out_13(n4bits_add_sous_5_out_13),
    .out_12(n4bits_add_sous_5_out_12), .in_3(n4bits_add_sous_4_out_12[0]),
    .in_5(n4bits_add_sous_4_out_12[1]), .in_7(n4bits_add_sous_4_out_12[2]), .in_9(n4bits_add_sous_4_out_12[3]));  // open: out_11
  not not_3 (not_3_out, in_1);
  _4Bits_Add__Sous u_4bits_add_sous_6 (
    .in_1(not_3_out), .in_2(or_2_out), .in_4(1'b0), .in_6(or_2_out), .in_8(1'b0), .in_10(1'b0),
    .out_15(n4bits_add_sous_6_out_15), .out_14(n4bits_add_sous_6_out_14), .out_13(n4bits_add_sous_6_out_13),
    .out_12(n4bits_add_sous_6_out_12), .in_3(n4bits_add_sous_1_out_12[0]),
    .in_5(n4bits_add_sous_1_out_12[1]), .in_7(n4bits_add_sous_1_out_12[2]), .in_9(n4bits_add_sous_1_out_12[3]));  // open: out_11
  not not_4 (not_4_out, in_1);
  _4Bits_Add__Sous u_4bits_add_sous_7 (
    .in_1(not_4_out), .in_2(or_3_out), .in_4(1'b0), .in_6(or_3_out), .in_8(1'b0), .in_10(1'b0),
    .out_15(n4bits_add_sous_7_out_15), .out_14(n4bits_add_sous_7_out_14), .out_13(n4bits_add_sous_7_out_13),
    .out_12(n4bits_add_sous_7_out_12), .in_3(n4bits_add_sous_2_out_12[0]),
    .in_5(n4bits_add_sous_2_out_12[1]), .in_7(n4bits_add_sous_2_out_12[2]), .in_9(n4bits_add_sous_2_out_12[3]));  // open: out_11
  _4Bits_Add__Sous u_4bits_add_sous_8 (
    .in_1(not_1_out), .in_2(or_4_out), .in_4(1'b0), .in_6(or_4_out), .in_8(1'b0), .in_10(1'b0),
    .out_15(n4bits_add_sous_8_out_15), .out_14(n4bits_add_sous_8_out_14), .out_13(n4bits_add_sous_8_out_13),
    .out_12(n4bits_add_sous_8_out_12), .in_3(n4bits_add_sous_3_out_12[0]),
    .in_5(n4bits_add_sous_3_out_12[1]), .in_7(n4bits_add_sous_3_out_12[2]), .in_9(n4bits_add_sous_3_out_12[3]));  // open: out_11
  Afficheur afficheur_2 (
    .in_1(n4bits_add_sous_5_out_12), .in_2(n4bits_add_sous_5_out_13), .in_3(n4bits_add_sous_5_out_14),
    .in_4(n4bits_add_sous_5_out_15), .a(out_4[6]), .b(out_4[5]), .out_7(out_4[4]), .d(out_4[3]),
    .out_9(out_4[2]), .out_10(out_4[1]), .out_11(out_4[0]));
  Afficheur afficheur_3 (
    .in_1(n4bits_add_sous_6_out_12), .in_2(n4bits_add_sous_6_out_13), .in_3(n4bits_add_sous_6_out_14),
    .in_4(n4bits_add_sous_6_out_15), .a(out_5[6]), .b(out_5[5]), .out_7(out_5[4]), .d(out_5[3]),
    .out_9(out_5[2]), .out_10(out_5[1]), .out_11(out_5[0]));
  Afficheur afficheur_4 (
    .in_1(n4bits_add_sous_7_out_12), .in_2(n4bits_add_sous_7_out_13), .in_3(n4bits_add_sous_7_out_14),
    .in_4(n4bits_add_sous_7_out_15), .a(out_6[6]), .b(out_6[5]), .out_7(out_6[4]), .d(out_6[3]),
    .out_9(out_6[2]), .out_10(out_6[1]), .out_11(out_6[0]));
  Afficheur afficheur_5 (
    .in_1(n4bits_add_sous_8_out_12), .in_2(n4bits_add_sous_8_out_13), .in_3(n4bits_add_sous_8_out_14),
    .in_4(n4bits_add_sous_8_out_15), .a(out_7[6]), .b(out_7[5]), .out_7(out_7[4]), .d(out_7[3]),
    .out_9(out_7[2]), .out_10(out_7[1]), .out_11(out_7[0]));
endmodule

module Comparateur_1_bit (
  input  x,
  input  y,
  output S,
  output Z
);

  wire and_2_out, and_3_out, not_1_out, not_2_out;

  not not_1 (not_1_out, x);
  not not_2 (not_2_out, y);
  and and_1 (S, x, not_2_out);
  and and_2 (and_2_out, not_1_out, not_2_out);
  and and_3 (and_3_out, x, y);
  or or_1 (Z, and_2_out, and_3_out);
endmodule

module Comparateur_2_bits (
  input  x1,
  input  x0,
  input  y1,
  input  y0,
  output S,
  output Z
);

  wire and_1_out, comparateur_1_bit_1_s, comparateur_1_bit_1_z, comparateur_1_bit_2_s, comparateur_1_bit_2_z;

  Comparateur_1_bit comparateur_1_bit_1 (.x(x1), .y(y1), .S(comparateur_1_bit_1_s), .Z(comparateur_1_bit_1_z));
  Comparateur_1_bit comparateur_1_bit_2 (.x(x0), .y(y0), .S(comparateur_1_bit_2_s), .Z(comparateur_1_bit_2_z));
  and and_1 (and_1_out, comparateur_1_bit_1_z, comparateur_1_bit_2_s);
  and and_2 (Z, comparateur_1_bit_1_z, comparateur_1_bit_2_z);
  or or_1 (S, comparateur_1_bit_1_s, and_1_out);
endmodule

module Comparateur_4_bits (
  input  x3,
  input  x2,
  input  x1,
  input  x0,
  output S,
  output Z
);

  wire and_1_out, comparateur_2_bits_1_s, comparateur_2_bits_1_z, comparateur_2_bits_2_s,
       comparateur_2_bits_2_z;

  Comparateur_2_bits comparateur_2_bits_1 (
    .x1(x3), .x0(x2), .y1(1'b1), .y0(1'b0), .S(comparateur_2_bits_1_s), .Z(comparateur_2_bits_1_z));
  Comparateur_2_bits comparateur_2_bits_2 (
    .x1(x1), .x0(x0), .y1(1'b0), .y0(1'b1), .S(comparateur_2_bits_2_s), .Z(comparateur_2_bits_2_z));
  and and_1 (and_1_out, comparateur_2_bits_1_z, comparateur_2_bits_2_s);
  and and_2 (Z, comparateur_2_bits_2_z, comparateur_2_bits_1_z);
  or or_1 (S, comparateur_2_bits_1_s, and_1_out);
endmodule

module Afficheur_16_bits (
  input  [15:0] in_1,
  output [13:0] out_2,
  output [13:0] out_3,
  output [13:0] out_4,
  output [13:0] out_5
);

  wire comparateur_4_bits_1_s, comparateur_4_bits_2_s, comparateur_4_bits_3_s, comparateur_4_bits_4_s,
       n4bits_add_sous_1_out_12, n4bits_add_sous_1_out_13, n4bits_add_sous_1_out_14,
       n4bits_add_sous_1_out_15, n4bits_add_sous_2_out_12, n4bits_add_sous_2_out_13,
       n4bits_add_sous_2_out_14, n4bits_add_sous_2_out_15, n4bits_add_sous_3_out_12,
       n4bits_add_sous_3_out_13, n4bits_add_sous_3_out_14, n4bits_add_sous_3_out_15,
       n4bits_add_sous_4_out_12, n4bits_add_sous_4_out_13, n4bits_add_sous_4_out_14,
       n4bits_add_sous_4_out_15, undriven, undriven_2, undriven_3, undriven_4, undriven_5, undriven_6,
       undriven_7;

  Comparateur_4_bits comparateur_4_bits_1 (
    .x3(in_1[3]), .x2(in_1[2]), .x1(in_1[1]), .x0(in_1[0]), .S(comparateur_4_bits_1_s));  // open: Z
  Afficheur afficheur_1 (
    .in_1(1'b0), .in_2(1'b0), .in_3(1'b0), .in_4(comparateur_4_bits_1_s), .a(out_2[13]), .b(out_2[12]),
    .out_7(out_2[11]), .d(out_2[10]), .out_9(out_2[9]), .out_10(out_2[8]), .out_11(out_2[7]));
  Comparateur_4_bits comparateur_4_bits_2 (
    .x3(in_1[7]), .x2(in_1[6]), .x1(in_1[5]), .x0(in_1[4]), .S(comparateur_4_bits_2_s));  // open: Z
  Afficheur afficheur_2 (
    .in_1(1'b0), .in_2(1'b0), .in_3(1'b0), .in_4(comparateur_4_bits_2_s), .a(out_3[13]), .b(out_3[12]),
    .out_7(out_3[11]), .d(out_3[10]), .out_9(out_3[9]), .out_10(out_3[8]), .out_11(out_3[7]));
  Comparateur_4_bits comparateur_4_bits_3 (
    .x3(in_1[11]), .x2(in_1[10]), .x1(in_1[9]), .x0(in_1[8]), .S(comparateur_4_bits_3_s));  // open: Z
  Afficheur afficheur_3 (
    .in_1(1'b0), .in_2(1'b0), .in_3(1'b0), .in_4(comparateur_4_bits_3_s), .a(out_4[13]), .b(out_4[12]),
    .out_7(out_4[11]), .d(out_4[10]), .out_9(out_4[9]), .out_10(out_4[8]), .out_11(out_4[7]));
  Comparateur_4_bits comparateur_4_bits_4 (
    .x3(in_1[15]), .x2(in_1[14]), .x1(in_1[13]), .x0(in_1[12]), .S(comparateur_4_bits_4_s));  // open: Z
  Afficheur afficheur_4 (
    .in_1(1'b0), .in_2(1'b0), .in_3(1'b0), .in_4(comparateur_4_bits_4_s), .a(out_5[13]), .b(out_5[12]),
    .out_7(out_5[11]), .d(out_5[10]), .out_9(out_5[9]), .out_10(out_5[8]), .out_11(out_5[7]));
  _4Bits_Add__Sous u_4bits_add_sous_1 (
    .in_1(1'b1), .in_2(comparateur_4_bits_1_s), .in_4(1'b0), .in_6(comparateur_4_bits_1_s), .in_8(1'b0),
    .in_10(1'b0), .out_15(n4bits_add_sous_1_out_15), .out_14(n4bits_add_sous_1_out_14),
    .out_13(n4bits_add_sous_1_out_13), .out_12(n4bits_add_sous_1_out_12), .in_3(in_1[3]), .in_5(in_1[2]),
    .in_7(in_1[1]), .in_9(in_1[0]));  // open: out_11
  Afficheur afficheur_5 (
    .in_1(n4bits_add_sous_1_out_12), .in_2(n4bits_add_sous_1_out_13), .in_3(n4bits_add_sous_1_out_14),
    .in_4(n4bits_add_sous_1_out_15), .a(out_2[6]), .b(out_2[5]), .out_7(out_2[4]), .d(out_2[3]),
    .out_9(out_2[2]), .out_10(out_2[1]), .out_11(out_2[0]));
  _4Bits_Add__Sous u_4bits_add_sous_2 (
    .in_1(1'b1), .in_2(comparateur_4_bits_2_s), .in_4(1'b0), .in_6(comparateur_4_bits_2_s), .in_8(1'b0),
    .in_10(1'b0), .out_15(n4bits_add_sous_2_out_15), .out_14(n4bits_add_sous_2_out_14),
    .out_13(n4bits_add_sous_2_out_13), .out_12(n4bits_add_sous_2_out_12), .in_3(in_1[7]), .in_5(in_1[6]),
    .in_7(in_1[5]), .in_9(in_1[4]));  // open: out_11
  Afficheur afficheur_6 (
    .in_1(n4bits_add_sous_2_out_12), .in_2(n4bits_add_sous_2_out_13), .in_3(n4bits_add_sous_2_out_14),
    .in_4(n4bits_add_sous_2_out_15), .a(out_3[6]), .b(out_3[5]), .out_7(out_3[4]), .d(out_3[3]),
    .out_9(out_3[2]), .out_10(out_3[1]), .out_11(out_3[0]));
  _4Bits_Add__Sous u_4bits_add_sous_3 (
    .in_1(1'b1), .in_2(comparateur_4_bits_3_s), .in_4(1'b0), .in_6(comparateur_4_bits_3_s), .in_8(1'b0),
    .in_10(1'b0), .out_15(n4bits_add_sous_3_out_15), .out_14(n4bits_add_sous_3_out_14),
    .out_13(n4bits_add_sous_3_out_13), .out_12(n4bits_add_sous_3_out_12), .in_3(in_1[11]), .in_5(in_1[10]),
    .in_7(in_1[9]), .in_9(in_1[8]));  // open: out_11
  Afficheur afficheur_7 (
    .in_1(n4bits_add_sous_3_out_12), .in_2(n4bits_add_sous_3_out_13), .in_3(n4bits_add_sous_3_out_14),
    .in_4(n4bits_add_sous_3_out_15), .a(out_4[6]), .b(out_4[5]), .out_7(out_4[4]), .d(out_4[3]),
    .out_9(out_4[2]), .out_10(out_4[1]), .out_11(out_4[0]));
  _4Bits_Add__Sous u_4bits_add_sous_4 (
    .in_1(1'b1), .in_2(comparateur_4_bits_4_s), .in_4(1'b0), .in_6(comparateur_4_bits_4_s), .in_8(1'b0),
    .in_10(1'b0), .out_15(n4bits_add_sous_4_out_15), .out_14(n4bits_add_sous_4_out_14),
    .out_13(n4bits_add_sous_4_out_13), .out_12(n4bits_add_sous_4_out_12), .in_3(in_1[15]), .in_5(in_1[14]),
    .in_7(in_1[13]), .in_9(in_1[12]));  // open: out_11
  Afficheur afficheur_8 (
    .in_1(n4bits_add_sous_4_out_12), .in_2(n4bits_add_sous_4_out_13), .in_3(n4bits_add_sous_4_out_14),
    .in_4(n4bits_add_sous_4_out_15), .a(out_5[6]), .b(out_5[5]), .out_7(out_5[4]), .d(out_5[3]),
    .out_9(out_5[2]), .out_10(out_5[1]), .out_11(out_5[0]));
  _7_Segment_Display u_7_segment_display_1 (
    .g(undriven_7), .f(undriven_2), .a(undriven_3), .b(undriven_5), .e(undriven), .d(undriven_6),
    .c(undriven_4));  // open: dp
endmodule
