// Logisim project composants.circ as structural Verilog: 3 circuits, main circuit demi add/sous
module demi_add_sous (
  input  A,
  input  B,
  input  C,
  output S,
  output Rs
);

  wire xor_1_out;

  xor xor_1 (xor_1_out, A, C);
  xor xor_2 (S, A, B);
  and and_1 (Rs, B, xor_1_out);
endmodule

module add_sous (
  input  C,
  input  A,
  input  B,
  input  Re,
  output S,
  output Rs
);

  wire demi_add_sous_1_rs, demi_add_sous_1_s, demi_add_sous_2_rs;

  demi_add_sous demi_add_sous_1 (.A(A), .B(B), .C(C), .S(demi_add_sous_1_s), .Rs(demi_add_sous_1_rs));
  demi_add_sous demi_add_sous_2 (.A(C), .B(Re), .C(demi_add_sous_1_s), .S(S), .Rs(demi_add_sous_2_rs));
  or or_1 (Rs, demi_add_sous_2_rs, demi_add_sous_1_rs);
endmodule

module add_sous_4_bits (
  input  a0,
  input  a1,
  input  a2,
  input  a3,
  input  b1,
  input  b2,
  input  b3,
  input  b0,
  input  com,
  output S0,
  output S3,
  output S1,
  output S2,
  output D
);

  wire add_sous_1_rs, add_sous_2_rs;

  add_sous add_sous_1 (.C(1'b0), .A(a0), .B(b0), .Re(com), .S(S0), .Rs(add_sous_1_rs));
  add_sous add_sous_2 (.C(add_sous_1_rs), .A(a1), .B(b1), .Re(com), .S(S1), .Rs(add_sous_2_rs));
  add_sous add_sous_3 (.C(add_sous_2_rs), .A(a2), .B(b2), .Re(com), .S(S2), .Rs(b3));
  add_sous add_sous_4 (.C(b3), .A(a3), .B(b3), .Re(com), .S(S3), .Rs(D));
endmodule
