// Logisim project composants2.circ as structural Verilog: 4 circuits, main circuit Module_Chiffre
module Module_Chiffre (
  input  A,
  input  B,
  input  C,
  input  D,
  output [6:0] out_5
);

  wire and_1_out, and_2_out, and_3_out, and_4_out, and_5_out, and_6_out, and_7_out, nand_1_out, nor_1_out,
       nor_2_out, not_1_out, not_2_out, not_3_out, not_4_out, not_5_out, not_6_out, not_7_out, not_8_out,
       or_1_out, or_2_out, or_3_out, xnor_1_out, xnor_2_out, xor_1_out;

  or u_a (out_5[0], A, C, xnor_1_out);
  xnor xnor_1 (xnor_1_out, D, B);
  nor nor_1 (nor_1_out, A, B);
  or u_b (out_5[1], A, nor_1_out, xnor_2_out);
  xnor xnor_2 (xnor_2_out, D, C);
  not not_1 (not_1_out, C);
  or u_c (out_5[2], D, not_1_out, B, A);
  not not_2 (not_2_out, B);
  and and_1 (and_1_out, not_2_out, or_1_out);
  or u_d (out_5[3], A, and_1_out, and_2_out, and_3_out);
  not not_3 (not_3_out, D);
  or or_1 (or_1_out, C, not_3_out);
  not not_4 (not_4_out, D);
  and and_2 (and_2_out, C, not_4_out);
  not not_5 (not_5_out, C);
  and and_3 (and_3_out, D, B, not_5_out);
  or or_2 (or_2_out, C, B);
  and and_4 (and_4_out, A, or_2_out);
  not not_6 (not_6_out, D);
  and and_5 (and_5_out, not_6_out, or_3_out);
  or e (out_5[4], and_4_out, and_5_out);
  not not_7 (not_7_out, B);
  or or_3 (or_3_out, C, not_7_out);
  and and_6 (and_6_out, B, nand_1_out);
  or f (out_5[5], A, and_6_out, nor_2_out);
  nand nand_1 (nand_1_out, D, C);
  nor nor_2 (nor_2_out, D, C);
  not not_8 (not_8_out, D);
  and and_7 (and_7_out, C, not_8_out);
  or g (out_5[6], A, and_7_out, xor_1_out);
  xor xor_1 (xor_1_out, C, B);
endmodule

module _1_2_add_sous (
  input  A,
  input  B,
  input  C,
  output S,
  output Rs
);

  wire xor_1_out;

  xor xor_1 (xor_1_out, A, C);
  xor xor_2 (S, A, B);
  and and_1 (Rs, B, xor_1_out);
endmodule

module add_sous (
  input  Re,
  input  A,
  input  B,
  input  C,
  output S,
  output Rs
);

  wire n1_2_add_sous_1_rs, n1_2_add_sous_1_s, n1_2_add_sous_2_rs;

  _1_2_add_sous u_1_2_add_sous_1 (.A(A), .B(B), .C(C), .S(n1_2_add_sous_1_s), .Rs(n1_2_add_sous_1_rs));
  _1_2_add_sous u_1_2_add_sous_2 (.A(n1_2_add_sous_1_s), .B(Re), .C(C), .S(S), .Rs(n1_2_add_sous_2_rs));
  or or_1 (Rs, n1_2_add_sous_2_rs, n1_2_add_sous_1_rs);
endmodule

module add_sous_4bit (
  input  a2,
  input  a0,
  input  a1,
  input  a3,
  input  b1,
  input  b2,
  input  b3,
  input  b0,
  input  com,
  output S0,
  output S1,
  output S2,
  output S3,
  output D
);

  wire add_sous_1_rs, add_sous_2_rs, add_sous_3_rs;

  add_sous add_sous_1 (.Re(1'b0), .A(a0), .B(b0), .C(com), .S(S0), .Rs(add_sous_1_rs));
  add_sous add_sous_2 (.Re(add_sous_1_rs), .A(a1), .B(b1), .C(com), .S(S1), .Rs(add_sous_2_rs));
  add_sous add_sous_3 (.Re(add_sous_2_rs), .A(a2), .B(b2), .C(com), .S(S2), .Rs(add_sous_3_rs));
  add_sous add_sous_4 (.Re(add_sous_3_rs), .A(a3), .B(b3), .C(com), .S(S3), .Rs(D));
endmodule
